# Fritzing sketch example_graphical_schematic (saved by Fritzing 0.9.4)
breadboards: 1

parts:
  Part1 = Arduino Uno (Rev3)
  R1 = TRIMPOT [package=3386u]
  LED1 = LED - 5mm [color="Red (633nm)" package="5 mm [THT]"]
  LED2 = LED - 5mm [color="Yellow (595nm)" package="5 mm [THT]"]
  R2 = Resistor [tolerance=±5% resistance=220 package=THT]
  R3 = Resistor [tolerance=±5% resistance=220 package=THT]

nets:
  N1: Part1.A0, R1.WIPER
  N2: Part1.GND, R1.CW, LED1.anode, LED2.anode
  N3: Part1.D2, R3.Pin_1
  N4: Part1.D6_PWM, R2.Pin_1
  N5: Part1.3V3, R1.CCW
  N6: LED1.cathode, R2.Pin_0
  N7: LED2.cathode, R3.Pin_0
